// Logisim project coaproject (1).circ as structural Verilog: 6 circuits, main circuit main
module main (
  input  [7:0] PC_in,
  input  [7:0] in_2,
  output [7:0] PC,
  output [15:0] out_4
);

  wire clock, not_1_out, not_2_out, PC_Shift_out, RESET;
  wire [3:0] CC;
  wire [7:0] MAR_q, RA_q, ram_1_data, RB_q, Reg_File_data_out__8_bits;
  wire [14:0] IR_q, MBR_q, rom_1_data;
  wire [15:0] RZ_q;

  PC u_PC (.PC_In(PC_in), .Clock(clock), .PC_Enable(PC_Shift_out), .Reset(RESET), .PC_Out(PC));
  Register MAR (.D(PC), .en(PC_Shift_out), .Q(MAR_q), .clk(clock), .clr(RESET));
  Shift_Register #(.length(5)) PC_Shift (
    .in(PC_Shift_out), .clk(clock), .out(PC_Shift_out));  // open: shift, load, clr, d0, q0, d1, q1, d2, q2, d3, q3, d4, q4
  Clock_Cycle clock_cycle_1 (.Clock(clock), .out_2(CC));
  Button button_1 (.out(RESET));
  ROM #(.dataWidth(15)) rom_1 (.addr(MAR_q), .data(rom_1_data));  // open: sel
  Clock clock_1 (.out(clock));
  not not_1 (not_1_out, PC_Shift_out);
  Hex_Digit_Display hex_digit_display_1 (.value(CC));  // open: dp
  Register #(.width(15)) MBR (.D(rom_1_data), .Q(MBR_q), .clk(clock), .clr(RESET));  // open: en
  Register #(.width(15)) IR (.D(MBR_q), .Q(IR_q), .clk(clock), .clr(RESET));  // open: en
  not not_2 (not_2_out, not_1_out);
  Register RA (.D(Reg_File_data_out__8_bits), .Q(RA_q), .clk(clock), .clr(RESET));  // open: en
  Reg_File Reg_File (
    .Data_in__8_bits(RZ_q[7:0]), .Rx__3_bits(IR_q[10:8]), .Clock(clock), .R_W_prime(not_1_out),
    .Data_out__8_bits(Reg_File_data_out__8_bits));
  RAM #(.bus("separate")) ram_1 (
    .addr(IR_q[7:0]), .din(RB_q), .data(ram_1_data), .str(not_2_out), .clk(clock), .ld(not_1_out));  // open: sel, clr
  Register RB (.D(ram_1_data), .Q(RB_q), .clk(clock), .clr(RESET));  // open: en
  Register #(.width(16)) RZ (.D(out_4), .Q(RZ_q), .clk(clock), .clr(RESET));  // open: en
  Hex_Digit_Display hex_digit_display_2 (.value(out_4[15:12]));  // open: dp
  ALU_8_Bit ALU (.A(RA_q), .B(in_2), .Opcode(IR_q[14:11]), .Output(out_4));
  Hex_Digit_Display hex_digit_display_3 (.value(out_4[11:8]));  // open: dp
  Hex_Digit_Display hex_digit_display_4 (.value(out_4[7:4]));  // open: dp
  Hex_Digit_Display hex_digit_display_5 (.value(out_4[3:0]));  // open: dp

  // Notes on the sheet:
  //   Code Memory
  //   contents of rom_1 (hex, n*v repeats v):
  //   201 c02 3b04 4003
  //   Data Memory
  //   Result
endmodule

// Reg
module Reg_File (
  input  [7:0] Data_in__8_bits,
  input  [2:0] Rx__3_bits,
  input  Clock,
  input  R_W_prime,
  output [7:0] Data_out__8_bits
);

  wire decoder_1_out0, decoder_1_out1, decoder_1_out2, decoder_1_out3, decoder_1_out4, decoder_1_out5,
       decoder_1_out6, decoder_1_out7, not_1_out;
  wire [7:0] R0_q, R1_q, R2_q, R3_q, R4_q, R5_q, R6_q, R7_q;

  Hex_Digit_Display hex_digit_display_1 (.value(Data_in__8_bits[3:0]));  // open: dp
  Hex_Digit_Display hex_digit_display_2 (.value(Data_in__8_bits[7:4]));  // open: dp
  Decoder #(.select(3), .disabled(0)) decoder_1 (
    .out0(decoder_1_out0), .out1(decoder_1_out1), .out2(decoder_1_out2), .out3(decoder_1_out3),
    .out4(decoder_1_out4), .out5(decoder_1_out5), .out6(decoder_1_out6), .out7(decoder_1_out7),
    .sel(Rx__3_bits), .en(not_1_out));
  not not_1 (not_1_out, R_W_prime);
  Register R0 (.D(Data_in__8_bits), .en(decoder_1_out0), .Q(R0_q), .clk(Clock));  // open: clr
  Register R1 (.D(Data_in__8_bits), .en(decoder_1_out1), .Q(R1_q), .clk(Clock));  // open: clr
  Register R2 (.D(Data_in__8_bits), .en(decoder_1_out2), .Q(R2_q), .clk(Clock));  // open: clr
  Register R3 (.D(Data_in__8_bits), .en(decoder_1_out3), .Q(R3_q), .clk(Clock));  // open: clr
  Register R4 (.D(Data_in__8_bits), .en(decoder_1_out4), .Q(R4_q), .clk(Clock));  // open: clr
  Register R5 (.D(Data_in__8_bits), .en(decoder_1_out5), .Q(R5_q), .clk(Clock));  // open: clr
  Register R6 (.D(Data_in__8_bits), .en(decoder_1_out6), .Q(R6_q), .clk(Clock));  // open: clr
  Register R7 (.D(Data_in__8_bits), .en(decoder_1_out7), .Q(R7_q), .clk(Clock));  // open: clr
  Hex_Digit_Display hex_digit_display_3 (.value(Data_out__8_bits[7:4]));  // open: dp
  Hex_Digit_Display hex_digit_display_4 (.value(Data_out__8_bits[3:0]));  // open: dp
  Multiplexer #(.select(3), .width(8)) multiplexer_1 (
    .in0(R0_q), .in1(R1_q), .in2(R2_q), .in3(R3_q), .in4(R4_q), .in5(R5_q), .in6(R6_q), .in7(R7_q),
    .out(Data_out__8_bits), .sel(Rx__3_bits), .en(R_W_prime));

  // Notes on the sheet:
  //   8-bit Register File (R0-R7)
endmodule

// ALU
module ALU_8_Bit (
  input  [7:0] A,
  input  [7:0] B,
  input  [3:0] Opcode,
  output [15:0] Output
);

  wire adder_1_cout, comparator_1_eq, comparator_1_gt, comparator_1_lt, subtractor_1_bout;
  wire [2:0] bit_extender_1_out;
  wire [3:0] bit_extender_12_out, bit_extender_13_out;
  wire [7:0] adder_1_out, and_1_out, bit_extender_2_out, bit_extender_3_out, bit_extender_14_out,
       divider_1_out, divider_1_rem, multiplier_1_cout, multiplier_1_out, nand_1_out, or_1_out,
       shifter_1_out, shifter_2_out, shifter_3_out, shifter_4_out, subtractor_1_out, xor_1_out;
  wire [15:0] bit_extender_4_out, bit_extender_5_out, bit_extender_6_out, bit_extender_7_out,
       bit_extender_8_out, bit_extender_9_out, bit_extender_10_out, bit_extender_11_out;

  Hex_Digit_Display hex_digit_display_1 (.value(A[7:4]));  // open: dp
  Hex_Digit_Display hex_digit_display_2 (.value(A[3:0]));  // open: dp
  Hex_Digit_Display hex_digit_display_3 (.value(B[7:4]));  // open: dp
  Hex_Digit_Display hex_digit_display_4 (.value(B[3:0]));  // open: dp
  Adder adder_1 (.a(A), .b(B), .out(adder_1_out), .cout(adder_1_cout));  // open: cin
  Subtractor subtractor_1 (.a(A), .b(B), .out(subtractor_1_out), .bout(subtractor_1_bout));  // open: bin
  Multiplier multiplier_1 (.a(A), .b(B), .out(multiplier_1_out), .cout(multiplier_1_cout));  // open: cin
  Divider divider_1 (.a(A), .b(B), .out(divider_1_out), .rem(divider_1_rem));  // open: upper
  assign and_1_out = A & B;  // AND_Gate and_1, 8 bits wide
  assign or_1_out = A | B;  // OR_Gate or_1, 8 bits wide
  assign nand_1_out = ~(A & B);  // NAND_Gate nand_1, 8 bits wide
  assign xor_1_out = A ^ B;  // XOR_Gate xor_1, 8 bits wide
  Bit_Extender #(.out_width(3)) bit_extender_1 (.in(B), .out(bit_extender_1_out));
  assign bit_extender_2_out = {{7{1'b0}}, adder_1_cout};  // Bit_Extender bit_extender_2
  assign bit_extender_3_out = {{7{1'b0}}, subtractor_1_bout};  // Bit_Extender bit_extender_3
  assign bit_extender_4_out = {{8{1'b0}}, and_1_out};  // Bit_Extender bit_extender_4
  assign bit_extender_5_out = {{8{1'b0}}, or_1_out};  // Bit_Extender bit_extender_5
  assign bit_extender_6_out = {{8{1'b0}}, nand_1_out};  // Bit_Extender bit_extender_6
  assign bit_extender_7_out = {{8{1'b0}}, xor_1_out};  // Bit_Extender bit_extender_7
  Shifter shifter_1 (.in(A), .\dist (bit_extender_1_out), .out(shifter_1_out));
  Shifter #(.shift("lr")) shifter_2 (.in(A), .\dist (bit_extender_1_out), .out(shifter_2_out));
  Shifter #(.shift("rl")) shifter_3 (.in(A), .\dist (bit_extender_1_out), .out(shifter_3_out));
  Shifter #(.shift("rr")) shifter_4 (.in(A), .\dist (bit_extender_1_out), .out(shifter_4_out));
  assign bit_extender_8_out = {{8{1'b0}}, shifter_1_out};  // Bit_Extender bit_extender_8
  assign bit_extender_9_out = {{8{1'b0}}, shifter_2_out};  // Bit_Extender bit_extender_9
  assign bit_extender_10_out = {{8{1'b0}}, shifter_3_out};  // Bit_Extender bit_extender_10
  assign bit_extender_11_out = {{8{1'b0}}, shifter_4_out};  // Bit_Extender bit_extender_11
  Comparator comparator_1 (.a(A), .b(B), .gt(comparator_1_gt), .eq(comparator_1_eq), .lt(comparator_1_lt));
  assign bit_extender_12_out = {{3{1'b0}}, comparator_1_gt};  // Bit_Extender bit_extender_12
  assign bit_extender_13_out = {{3{1'b0}}, comparator_1_eq};  // Bit_Extender bit_extender_13
  assign bit_extender_14_out = {{7{1'b0}}, comparator_1_lt};  // Bit_Extender bit_extender_14
  Hex_Digit_Display hex_digit_display_5 (.value(Output[15:12]));  // open: dp
  Hex_Digit_Display hex_digit_display_6 (.value(Output[11:8]));  // open: dp
  Hex_Digit_Display hex_digit_display_7 (.value(Output[7:4]));  // open: dp
  Hex_Digit_Display hex_digit_display_8 (.value(Output[3:0]));  // open: dp
  Multiplexer #(.select(4), .width(16), .enable("false")) multiplexer_1 (
    .in0({bit_extender_2_out, adder_1_out}), .in1({bit_extender_3_out, subtractor_1_out}),
    .in2({multiplier_1_cout, multiplier_1_out}), .in3({divider_1_rem, divider_1_out}),
    .in4(bit_extender_4_out), .in5(bit_extender_5_out), .in6(bit_extender_6_out), .in7(bit_extender_7_out),
    .in8(bit_extender_8_out), .in9(bit_extender_9_out), .in10(bit_extender_10_out),
    .in11(bit_extender_11_out), .in12({bit_extender_14_out, bit_extender_13_out, bit_extender_12_out}),
    .out(Output), .sel(Opcode));  // open: in13, in14, in15
endmodule

module PC (
  input  [7:0] PC_In,
  input  Clock,
  input  PC_Enable,
  input  Reset,
  output [7:0] PC_Out
);

  wire [7:0] adder_1_out;

  Adder adder_1 (.a(PC_In), .b(PC_Out), .out(adder_1_out), .cin(1'b1));  // open: cout
  Hex_Digit_Display hex_digit_display_1 (.value(PC_Out[7:4]));  // open: dp
  Register register_1 (.D(adder_1_out), .en(PC_Enable), .Q(PC_Out), .clk(Clock), .clr(Reset));
  Hex_Digit_Display hex_digit_display_2 (.value(PC_Out[3:0]));  // open: dp
endmodule

module Clock_Cycle (
  input  Clock,
  output [3:0] out_2
);

  Counter #(.width(4), .max('h4)) counter_1 (.Q(out_2), .clk(Clock));  // open: load, D, count, carry, clr
endmodule

module Integration_10_Jan (
  input  [7:0] PC_in,
  output [7:0] out_2
);

  wire [7:0] IR_q, MAR_q, ram_1_data;
  wire [14:0] MBR_q, rom_1_data;
  wire [14:8] IR_q_2;

  PC pc_1 (.PC_In(PC_in), .PC_Out(out_2));  // open: Clock, PC_Enable, Reset
  Register MAR (.D(out_2), .Q(MAR_q));  // open: en, clk, clr
  ROM #(.dataWidth(15)) rom_1 (.addr(MAR_q), .data(rom_1_data));  // open: sel
  RAM #(.bus("separate")) ram_1 (.din(IR_q), .data(ram_1_data));  // open: addr, str, sel, clk, ld, clr
  Register #(.width(15)) IR (.D(MBR_q), .Q({IR_q_2, IR_q}));  // open: en, clk, clr
  Register #(.width(15)) MBR (.D(rom_1_data), .Q(MBR_q));  // open: en, clk, clr
  Register RA ();  // open: D, en, Q, clk, clr
  Register register_1 ();  // open: D, en, Q, clk, clr
  Register RB ();  // open: D, en, Q, clk, clr
  Reg_File reg_file_1 (.Rx__3_bits(IR_q_2[10:8]));  // open: Data_in__8_bits, Clock, R_W_prime, Data_out__8_bits
  ALU_8_Bit alu_8_bit_1 (.B(ram_1_data));  // open: A, Opcode, Output

  // Notes on the sheet:
  //   Code memory
  //   Data memory
endmodule
